# Fritzing sketch ProjetoLola (saved by Fritzing 0.9.3b)
breadboards: 2

parts:
  R1 = Resistor [tolerance=±5% resistance=220 package=THT]
  R2 = Resistor [tolerance=±5% resistance=220 package=THT]
  LED1 = LED - 5mm [color="Blue (525nm)" package="5 mm [THT]"]
  LED2 = LED - 5mm [color="Blue (525nm)" package="5 mm [THT]"]
  J1 = Basic Servo
  J2 = Basic Servo
  Componente1 = Arduino Uno (Rev3)
  Componente2 = Adafruit TCS34725 RGB Color Sensor [part_number="Adafruit #1334"]

nets:
  N1: R1.Pin_0, LED1.cathode
  GND: R1.Pin_1, R2.Pin_1, J1.gnd, J2.gnd, Componente1.GND, Componente2.GND
  N2: R2.Pin_0, LED2.cathode
  N3: LED1.anode, LED2.anode, Componente1.D11_PWM/MOSI
  VCC: J1.vcc, J2.vcc, Componente1.5V, Componente2.+3V3
  N4: J1.pulse, J2.pulse, Componente1.D9_PWM
  N5: Componente1.A4/SDA, Componente2.SDA
  N6: Componente1.A5/SCL, Componente2.SCL

custom parts:
  Adafruit TCS34725 RGB Color Sensor: Your electronics can now see in dazzling color with this lovely color light sensor. We found the best color sensor on the market, the TCS34725, which has RGB and Clear light sensing elements. An IR blocking filter, integrated on-chip and localized to the color sensing photodiodes, minimizes the IR spectral component of the incoming light and allows color measurements to be made accurately. The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
