# Fritzing sketch Camaleão Arco-íris (saved by Fritzing 0.9.3b)
breadboards: 1

parts:
  R2 = Resistor [tolerance=±5% resistance=220 package=THT]
  Componente1 = Arduino Nano (Rev3.0)
  U1 = TCRT5000 [package=THT]
  R5 = Resistor [tolerance=±5% resistance=10k package=THT]
  LED4 = RGB LED (com. cathode, rgb) [package="5 mm [THT]"]
  R13 = Resistor [tolerance=±5% resistance=2.2k package=THT]
  R14 = Resistor [tolerance=±5% resistance=2.2k package=THT]
  R15 = Resistor [tolerance=±5% resistance=2.2k package=THT]

nets:
  N1: R2.Pin_0, Componente1.5V, R5.Pin_0
  N2: R2.Pin_1, U1.Pin_4
  N3: Componente1.GND, U1.Pin_2, U1.Pin_3, LED4.green_anode
  N4: Componente1.D2, U1.Pin_1, R5.Pin_1
  N5: Componente1.D3, R13.Pin_0
  N6: Componente1.D4, R14.Pin_0
  N7: Componente1.D5, R15.Pin_0
  N8: LED4.red_anode, R15.Pin_1
  N9: LED4.common_cathode, R14.Pin_1
  N10: LED4.blue_anode, R13.Pin_1

custom parts:
  TCRT5000: TCRT5000 optical reflective sensor

// code stored in the sketch: camaleaoArcoiris.ino
const int r = 3;      //Declarando o pino red do led rgb
const int g = 4;      //Declarando o pino green do led rgb
const int b = 5;      //Declarando o pino blue do led rgb
int pinosensor = 2;   //Ligado ao pino "coletor" do sensor óptico
int leitura;          //Armazena informações sobre a leitura do sensor
int count = 0;        //Declara o contador
void setup()
{

  //definindo saida 
  pinMode(r, OUTPUT);
  pinMode(g, OUTPUT);
  pinMode(g, OUTPUT);

  //Definindo entrada
  pinMode(pinosensor, INPUT);   //Define o pino do sensor como entrada
  Serial.begin(9600);
}

void loop()
{
  //Le as informações do pino do sensor
  leitura = digitalRead(pinosensor);
  if (leitura != 1) {

    //Condição para led = vermelho
    if (count == 1) {
      digitalWrite(r, 1);
      digitalWrite(g, 0);
      digitalWrite(b, 0);
    }
    //Condçao para led = verde
    if (count == 2) {
      digitalWrite(r, 0);
      digitalWrite(g, 1);
      digitalWrite(b, 0);
    }
    //Condição para led = azul
    if (count == 3) {
      
      count = 0;              //Zerando o contador

      digitalWrite(r, 0);
      digitalWrite(g, 0);
      digitalWrite(b, 1);
    }

    count++;                  //Soma + 1 ao contador
    Serial.println(count);    //Imprime contador

    delay(300);               //Espera
  }
}
