# Fritzing sketch Projeto de eletronica frietzing (saved by Fritzing 0.9.3b)
breadboards: 1

parts:
  U1 = TCRT5000
  R1 = Resistor [tolerance=±5% resistance=330 package=THT]
  R2 = Resistor [tolerance=±5% resistance=33k package=THT]
  Componente1 = Arduino Uno (Rev3)
  LED1 = smd LED [color="Red (633nm)" package="0805 [SMD]"]
  LED2 = smd LED [color="Red (633nm)" package="0805 [SMD]"]
  R3 = Resistor [tolerance=±5% resistance=220 package=THT]
  R4 = Resistor [tolerance=±5% resistance=220 package=THT]
  M1 = DC Motor

nets:
  N1: U1.connector0, R2.Pin_1, Componente1.D7
  N2: U1.connector1, U1.connector2, Componente1.GND, LED1.cathode, LED2.cathode, M1.pin_1
  N3: U1.connector3, R1.Pin_1
  N4: R1.Pin_0, R2.Pin_0, Componente1.5V
  N5: Componente1.D12/MISO, R3.Pin_0
  N6: Componente1.D13/SCK, R4.Pin_0
  N7: Componente1.D3_PWM, M1.pin_2
  N8: LED1.anode, R4.Pin_1
  N9: LED2.anode, R3.Pin_1
