# Fritzing sketch Projeto arduino - Shield (saved by Fritzing 0.9.3b)
circuit board: 5.66757cm x 5.75901cm
breadboards: 2

parts:
  hc-sr1 = hc-sr04
  J1 = female pin header, 2 pins [form="♀ (female)"]
  J2 = female pin header, 2 pins [form="♀ (female)"]
  J3 = XT60 Connector [package=THT]
  J4 = female pin header, 4 pins [form="♀ (female)"]
  J6 = female pin header, 3 pins [form="♀ (female)"]
  J5 = female pin header, 3 pins [form="♀ (female)"]
  Componente1 = Arduino Uno (Rev3)

nets (from the pcb view):
  VCC: hc-sr1.VCC, J6.pin2, J5.pin2, Componente1.5V
  N1: hc-sr1.Trig, Componente1.A4/SDA
  N2: hc-sr1.Echo, Componente1.A5/SCL
  N3: J1.pin2, J2.pin1, Componente1.VIN
  N4: J2.pin2, J3.VCC
  GND: J3.GND, Componente1.GND
  N5: J4.pin1, Componente1.D7
  N6: J4.pin2, Componente1.D6_PWM
  N7: J4.pin3, Componente1.D5_PWM
  N8: J4.pin4, Componente1.D4
  N9: J6.pin3, J5.pin3, Componente1.D9_PWM

notes:
  Conector - Alimetação
  Interruptor
  Ponte H - Alimentação
  Ponte H - Motores DC
  Servos Motores
  FIOS :
  *Preto - GND
  *Vermelho - 5v
  *Laranja - ALIMENTAÇÃO

custom parts:
  XT60 Connector: Yellow XT60 connector for high current loads up to 40A
