# Fritzing sketch Protoboard_Slide (saved by Fritzing 0.9.3b)
breadboards: 1

parts:
  M1 = DC Motor
  M2 = DC Motor
  Componente1 = Arduino Uno (Rev3) - ICSP
  S1 = H-Bridge with L298N
  VCC1 = Battery block 9V
  hc-sr2 = hc-sr04
  J1 = Basic Servo

nets:
  N1: M1.pin_1, S1.OUT4-Motor2
  N2: M1.pin_2, S1.OUT3-Motor2
  N3: M2.pin_1, S1.OUT1-Motor1
  N4: M2.pin_2, S1.OUT2-Motor1
  N5: Componente1.A4/SDA, hc-sr2.Trig
  N6: Componente1.A5/SCL, hc-sr2.Echo
  VCC: Componente1.5V, hc-sr2.VCC, J1.vcc
  N7: Componente1.D9_PWM, J1.pulse
  GND: Componente1.GND, S1.GND, VCC1.-, hc-sr2.GND, J1.gnd
  N8: Componente1.D4, S1.IN4
  N9: Componente1.D5_PWM, S1.IN3
  N10: Componente1.D6_PWM, S1.IN2
  N11: Componente1.D7, S1.IN1
  VIN: Componente1.VIN, S1.12V, VCC1.+

custom parts:
  H-Bridge with L298N: h-bridge
