# Fritzing sketch Fritizing_salem (saved by Fritzing 0.9.3b)
circuit board: 2.89441cm x 2.83341cm
circuit board: 7.65626cm x 5.3888cm
breadboards: 2

parts:
  R1 = Resistor [tolerance=±5% resistance=220 package=THT]
  LED_RGB = RGB LED (com. cathode, rgb) [package="5 mm [THT]"]
  R2 = Resistor [tolerance=±5% resistance=220 package=THT]
  R3 = Resistor [tolerance=±5% resistance=220 package=THT]
  Conector2 = female pin header, 3 pins [form="♀ (female)"]
  R4 = Resistor [tolerance=±5% resistance=220 package=THT]
  LED_RGB_2 = RGB LED (com. cathode, rgb) [package="5 mm [THT]"]
  Arduino_Uno = Arduino Uno (Rev3)
  garra = Basic Servo
  calda = Basic Servo
  Sonar = hc-sr04
  J1 = female pin header, 3 pins [form="♀ (female)"]
  Power_plug1 = Power plug

nets:
  N1: R1.Pin_0, R3.Pin_0, Conector2.pin2
  N2: R1.Pin_1, LED_RGB.blue_anode
  N3: LED_RGB.red_anode, R4.Pin_1
  GND: LED_RGB.common_cathode, Conector2.pin3, LED_RGB_2.common_cathode, Arduino_Uno.GND, garra.gnd, calda.gnd, Sonar.GND, J1.pin3, Power_plug1.GND
  N4: R2.Pin_0, Conector2.pin1, R4.Pin_0
  N5: R2.Pin_1, LED_RGB_2.red_anode
  N6: R3.Pin_1, LED_RGB_2.blue_anode
  N7: Arduino_Uno.A4/SDA, Sonar.Trig
  N8: Arduino_Uno.A5/SCL, Sonar.Echo
  N9: Arduino_Uno.D10_PWM/SS, garra.pulse
  N10: Arduino_Uno.D11_PWM/MOSI, calda.pulse
  N11: Arduino_Uno.D6_PWM, J1.pin2
  N12: Arduino_Uno.D7, J1.pin1
  5V: Arduino_Uno.5V, garra.vcc, calda.vcc, Sonar.VCC, Power_plug1.VCC

notes:
  --- CORES DOS FIOS ---
  VCC - vermelho
  GND- preto
  echo pin A5 (verde)
  trig pin A4 (lilás)
  Sinal - amarelo
  Servo garra pin~10
  Servo calda pin~11
  RGB(B)- pin 6 (azul)
  RGB(R)- pin 7 (laranja)
