# Fritzing sketch foca (saved by Fritzing 0.9.3b)
circuit board: 7.63292cm x 7.68308cm
breadboards: 2

parts:
  Componente1 = Arduino Uno (Rev3)
  J2 = Basic Servo
  LED1 = LED - 5mm [color="Blue (430nm)" package="5 mm [THT]"]
  Componente2 = RFID-RC522-v3
  LED2 = LED - 5mm [color="Blue (430nm)" package="5 mm [THT]"]
  R3 = Resistor [tolerance=±5% resistance=220 package=THT]
  J1 = Basic Servo
  R2 = Resistor [tolerance=±5% resistance=220 package=THT]
  R1 = Photocell (LDR) [package=THT]
  R4 = Resistor [tolerance=±5% resistance=220 package=THT]
  J3 = female pin header, 5 pins [form="♀ (female)"]

nets (from the breadboard view):
  N1: Componente1.A0, R2.Pin_0, R1.pin_1
  N2: Componente1.D8, LED1.anode
  N3: Componente1.D5_PWM, J1.pulse
  N4: Componente1.D6_PWM, J2.pulse
  N5: Componente1.D7, LED2.anode
  VCC: Componente1.3V3, J2.vcc, Componente2.3.3V, J1.vcc
  N6: Componente1.5V, R1.pin_0
  GND: Componente1.GND, J2.gnd, R3.Pin_1, J1.gnd, R2.Pin_1, R4.Pin_1
  N7: LED1.cathode, R4.Pin_0
  N8: Componente2.SDA, J3.pin2
  N9: Componente2.SCK, J3.pin5
  N10: Componente2.MOSI, J3.pin3
  N11: Componente2.MISO, J3.pin4
  N12: Componente2.RST, J3.pin1
  N13: LED2.cathode, R3.Pin_0

custom parts:
  RFID-RC522-v3: A simple China made RFID-RC522 Reader (6x4 cm); do check the pin labels, as this is a MFRC522 based clone.
