# Fritzing sketch Projeto_Final_Arduino (saved by Fritzing 0.9.0b)
circuit board: 7.44054cm x 5.33924cm
breadboards: 1

parts:
  LED1 = LED - 5mm [color="Red (633nm)" package="5 mm [THT]"]
  LED2 = LED - 5mm [color="Red (633nm)" package="5 mm [THT]"]
  R1 = Resistor [tolerance=±5% resistance=220 package=THT]
  R2 = Resistor [tolerance=±5% resistance=220 package=THT]
  Part1 = HC-SR04 Ultrasonic Rangemeter
  Componente1 = Arduino Nano (Rev3.0)
  J1 = Piezo Speaker

nets:
  GND: LED1.cathode, LED2.cathode, Part1.GND, Componente1.GND, J1.pin1
  N1: LED1.anode, R1.Pin_1, Componente1.D12/MISO
  N2: LED2.anode, R2.Pin_1, Componente1.D11/MOSI
  VCC: R1.Pin_0, R2.Pin_0, Part1.VCC, Componente1.5V
  N3: Part1.Trig, Componente1.D4
  N4: Part1.Echo, Componente1.A1
  N5: Componente1.D2, J1.pin2
