# Fritzing sketch FritzingNOVO (saved by Fritzing 0.9.3b)
breadboards: 1

parts:
  Componente1 = Arduino Uno (Rev3)
  J2 = Basic Servo
  J3 = Basic Servo
  LED2 = smd LED [color="Red (633nm)" package="1206 [SMD]"]
  LED3 = smd LED [color="Red (633nm)" package="1206 [SMD]"]
  R3 = Resistor [tolerance=±5% resistance=220 package="2010 [SMD]"]
  Componente2 = SRF05 Ultrasonic Rangefinder
  R2 = Resistor [tolerance=±5% resistance=220 package="2010 [SMD]"]

nets:
  N1: Componente1.A4/SDA, Componente2.Trig
  N2: Componente1.A5/SCL, Componente2.Echo
  N3: Componente1.D9_PWM, J2.pulse
  N4: Componente1.D11_PWM/MOSI, J3.pulse
  5V: Componente1.5V, J2.vcc, J3.vcc, LED2.anode, LED3.anode, Componente2.VCC
  GND: Componente1.GND, J2.gnd, J3.gnd, R3.Pin_0, Componente2.GND, R2.Pin_0
  N5: LED2.cathode, R2.Pin_1
  N6: LED3.cathode, R3.Pin_1
