# Fritzing sketch BolaDeOuroF (saved by Fritzing 0.9.3b)
circuit board: 7.97372cm x 6.35519cm
breadboards: 1

parts:
  R1 = Resistor [tolerance=±5% resistance=220 package=THT]
  LED1 = LED - 5mm [color="Red (633nm)" package="5 mm [THT]"]
  R2 = Resistor [tolerance=±5% resistance=220 package=THT]
  LED2 = LED - 5mm [color="Red (633nm)" package="5 mm [THT]"]
  J1 = Basic Servo
  Componente1 = Arduino Uno (Rev3) - ICSP
  FC-1 = Sound Sensor

nets:
  N1: R1.Pin_0, Componente1.D2
  N2: R1.Pin_1, LED2.anode
  GND: LED1.cathode, LED2.cathode, J1.gnd, Componente1.GND, FC-1.GND
  N3: LED1.anode, R2.Pin_1
  N4: R2.Pin_0, Componente1.D4
  VCC: J1.vcc, Componente1.5V, FC-1.VCC
  N5: J1.pulse, Componente1.D9_PWM
  N6: Componente1.A0, FC-1.OUT
