# Fritzing sketch frizLucinha (saved by Fritzing 0.9.3b)
breadboards: 1

parts:
  U1 = TCRT5000 [package=THT]
  R1 = Resistor [tolerance=±5% resistance=330 package=THT]
  R2 = Resistor [tolerance=±5% resistance=220 package=THT]
  R3 = Resistor [tolerance=±5% resistance=220 package=THT]
  LED1 = LED - 5mm [color="Red (633nm)" package="5 mm [THT]"]
  LED2 = LED - 5mm [color="Red (633nm)" package="5 mm [THT]"]
  J1 = Piezo Speaker
  J2 = Basic Servo
  R4 = Resistor [tolerance=±5% resistance=10k package=THT]
  Componente1 = Arduino Uno (Rev3)

nets:
  N1: U1.Pin_1, R4.Pin_1, Componente1.A0
  GND: U1.Pin_2, U1.Pin_3, R2.Pin_0, R3.Pin_0, J1.pin1, J2.gnd, Componente1.GND
  N2: U1.Pin_4, R1.Pin_0
  VCC: R1.Pin_1, J2.vcc, R4.Pin_0, Componente1.5V
  N3: R2.Pin_1, LED1.cathode
  N4: R3.Pin_1, LED2.cathode
  N5: LED1.anode, LED2.anode, Componente1.D6_PWM
  N6: J1.pin2, Componente1.D10_PWM/SS
  N7: J2.pulse, Componente1.D9_PWM

custom parts:
  TCRT5000: TCRT5000 optical reflective sensor
