# Fritzing sketch PROTOTIPO PIKACHU ARDUINO NANO (saved by Fritzing 0.9.3b)
circuit board: 6.02822cm x 4.35344cm
breadboards: 4

parts:
  Modulo_Bluetooth = female pin header, 4 pins [form="♀ (female)"]
  R1 = Resistor [tolerance=±5% resistance=1.5k package=THT]
  R2 = Resistor [tolerance=±5% resistance=2.2k package=THT]
  Led_RGB = female pin header, 4 pins [form="♀ (female)"]
  LED_3 = female pin header, 2 pins [form="♀ (female)"]
  LED_4 = female pin header, 2 pins [form="♀ (female)"]
  Arduino_Nano = Arduino Nano (Rev3.0)
  LED_2 = female pin header, 2 pins [form="♀ (female)"]
  LED_1 = female pin header, 2 pins [form="♀ (female)"]
  Fonte_Ponte_H = female pin header, 2 pins [form="♀ (female)"]
  Interruptor = female pin header, 2 pins [form="♀ (female)"]
  Ponte_H = female pin header, 4 pins [form="♀ (female)"]
  Alimentação = female pin header, 2 pins [form="♀ (female)"]
  Servo = female pin header, 3 pins [form="♀ (female)"]

nets:
  N1: Modulo_Bluetooth.pin1, R1.Pin_1, R2.Pin_0
  N2: Modulo_Bluetooth.pin2, Arduino_Nano.D1/TX
  N3: Modulo_Bluetooth.pin3, R2.Pin_1, Led_RGB.pin3, LED_3.pin2, LED_4.pin2, Arduino_Nano.GND, LED_2.pin2, LED_1.pin2, Fonte_Ponte_H.pin1, Alimentação.pin2, Servo.pin3
  N4: Modulo_Bluetooth.pin4, Arduino_Nano.5V, Servo.pin2
  N5: R1.Pin_0, Arduino_Nano.D0/RX
  N6: Led_RGB.pin1, Arduino_Nano.D8
  N7: Led_RGB.pin2, Arduino_Nano.D9
  N8: Led_RGB.pin4, Arduino_Nano.D10
  N9: LED_3.pin1, Arduino_Nano.D11/MOSI
  N10: LED_4.pin1, Arduino_Nano.D12/MISO
  N11: Arduino_Nano.D2, LED_1.pin1
  N12: Arduino_Nano.D3, LED_2.pin1
  N13: Arduino_Nano.D4, Ponte_H.pin1
  N14: Arduino_Nano.D5, Ponte_H.pin2
  N15: Arduino_Nano.D6, Ponte_H.pin3
  N16: Arduino_Nano.D7, Ponte_H.pin4
  N17: Arduino_Nano.VIN, Fonte_Ponte_H.pin2, Interruptor.pin1
  N18: Arduino_Nano.D13/SCK, Servo.pin1
  N19: Interruptor.pin2, Alimentação.pin1

notes:
  Led RGB:
  Red - Pino 6
  Green - Pino 7
  Blue - Pino 8
  PINAGEM:
  Leds Auxiliares:
  Led 1 - Pino 2
  Led 2 - Pino 3
  Led 3 - Pino 11
  Led 4 - Pino 12
  Modulo Bluetooth:
  RX - Pino 0
  TX - Pino 1
  Senha: 1605
  Ponte H: (Pinagem Modificada)
  Pino 4 - Pino 5
  Pino 5 - Pino 4
  Pino 6 - Pino 6
  Pino 7 - Pino 7
