# Fritzing sketch Fritzing - Robô eletrônica (saved by Fritzing 0.9.0b)
breadboards: 1

parts:
  R1 = Resistor [tolerance=±5% resistance=33k package=THT]
  R2 = Resistor [tolerance=±5% resistance=330 package=THT]
  U1 = TCRT5000 [package=THT]
  Componente1 = Arduino Uno (Rev3)
  J1 = Basic Servo
  J2 = Basic Servo

nets:
  N1: R1.Pin_0, U1.Pin_1, Componente1.A0
  VCC: R1.Pin_1, R2.Pin_1, Componente1.5V, J1.vcc, J2.vcc
  N2: R2.Pin_0, U1.Pin_4
  GND: U1.Pin_2, U1.Pin_3, Componente1.GND, J1.gnd, J2.gnd
  N3: Componente1.D9_PWM, J1.pulse, J2.pulse

notes:
  SERVO:
  - Fio amarelo = porta 9
  - Fio vermelho = 5V
  - Fio preto = GND
  -------------------------------
  Porta A0 = Fio ciano

custom parts:
  TCRT5000: TCRT5000 optical reflective sensor
