# Fritzing sketch Fritizing K_L_K (saved by Fritzing 0.9.3b)
breadboards: 1

parts:
  Componente1 = Arduino Uno (Rev3)
  J1 = Piezo Speaker
  U1 = TCRT5000 [package=THT]
  R1 = Resistor [tolerance=±5% resistance=330 package="0805 [SMD]"]
  R2 = Resistor [tolerance=±5% resistance=220 package="0805 [SMD]"]
  R3 = Resistor [tolerance=±5% resistance=10k package="0805 [SMD]"]

nets:
  N1: Componente1.A0, U1.Pin_3, R3.Pin_1
  N2: Componente1.D10_PWM/SS, J1.pin2, R2.Pin_1
  N3: Componente1.GND, J1.pin1, U1.Pin_1, U1.Pin_4, R2.Pin_0
  N4: Componente1.5V, R1.Pin_1, R3.Pin_0
  N5: U1.Pin_2, R1.Pin_0

custom parts:
  TCRT5000: TCRT5000 optical reflective sensor
