# Fritzing sketch P_eletronica (saved by Fritzing 0.9.3b)
breadboards: 1

parts:
  e-radionica1 = TCS230 Color Sensor [part_number=101209]
  Componente1 = Arduino Uno (Rev3)
  J1 = Basic Servo
  J2 = Basic Servo
  R1 = Resistor [tolerance=±5% resistance=220 package=THT]
  R2 = Resistor [tolerance=±5% resistance=220 package=THT]
  LED1 = LED - 5mm [color="Red (633nm)" package="5 mm [THT]"]
  LED2 = LED - 5mm [color="Red (633nm)" package="5 mm [THT]"]

nets:
  GND: e-radionica1.Gnd, Componente1.GND, J1.gnd, J2.gnd, R1.Pin_1, R2.Pin_1
  N1: e-radionica1.OE, e-radionica1.S2, Componente1.D12/MISO
  N2: e-radionica1.S1, Componente1.D9_PWM
  N3: e-radionica1.S0, Componente1.D8
  N4: e-radionica1.S3, Componente1.D11_PWM/MOSI
  N5: e-radionica1.Out, Componente1.D10_PWM/SS
  VCC: e-radionica1.Vcc, Componente1.5V, J1.vcc, J2.vcc
  N6: Componente1.D2, LED1.anode, LED2.anode
  N7: Componente1.D6_PWM, J1.pulse
  N8: Componente1.D7, J2.pulse
  N9: R1.Pin_0, R2.Pin_0, LED1.cathode, LED2.cathode

custom parts:
  TCS230 Color Sensor: TCS230
